// Logisim project alu.circ as structural Verilog: 8 circuits, main circuit main
module main (
  input  [31:0] X,
  input  [31:0] Y,
  input  [5:0] Switch__S,
  output Signed_Overflow,
  output [31:0] RESULT,
  output Equal
);

  wire add_1_overflow, adder_1_cout, multiplexer_1_out, multiplexer_5_out, sub_1_overflow, subtractor_1_bout;
  wire [4:0] bit_extender_1_out;
  wire [31:0] _00, _02, _2a, _2b, _03, _3e, _3f, _20, _21, _22, _23, _24, _25, jr, multiplexer_2_out,
       multiplexer_3_out, multiplexer_4_out;

  Bit_Extender #(.in_width(32), .out_width(5)) bit_extender_1 (.in(Y), .out(bit_extender_1_out));
  Shifter #(.width(32)) shifter_1 (.in(X), .\dist (bit_extender_1_out), .out(_00));
  Shifter #(.width(32), .shift("lr")) shifter_2 (.in(X), .\dist (bit_extender_1_out), .out(_02));
  Shifter #(.width(32), .shift("ar")) shifter_3 (.in(X), .\dist (bit_extender_1_out), .out(_03));
  add add_1 (.X(X), .Y(Y), .overflow(add_1_overflow), .out(_20));
  Adder #(.width(32)) adder_1 (.a(X), .b(Y), .out(_21), .cout(adder_1_cout));  // open: cin
  sub sub_1 (.X(X), .Y(Y), .overflow(sub_1_overflow), .result(_22));
  Subtractor #(.width(32)) subtractor_1 (.a(X), .b(Y), .out(_23), .bout(subtractor_1_bout));  // open: bin
  Subtractor #(.width(32)) subtractor_2 (.a(X), .b(32'h100000), .out(jr));  // open: bin, bout
  assign _24 = X & Y;  // AND_Gate and_1, 32 bits wide
  assign _25 = X | Y;  // OR_Gate or_1, 32 bits wide
  slt slt_1 (.X(X), .Y(Y), .out(_2a));
  sltu sltu_1 (.X(X), .Y(Y), .out(_2b));
  equal equal_1 (.X(X), .Y(Y), .out(Equal));
  bitpal bitpal_1 (.X(X), .out(_3e));
  lfsr lfsr_1 (.in_1(X), .out(_3f));
  Multiplexer #(.select(2)) multiplexer_1 (
    .in0(add_1_overflow), .in1(adder_1_cout), .in2(sub_1_overflow), .in3(subtractor_1_bout),
    .out(multiplexer_1_out), .sel(Switch__S[1:0]));  // open: en
  Multiplexer #(.select(2), .width(32)) multiplexer_2 (
    .in0(_00), .in2(_20), .out(multiplexer_2_out), .sel(Switch__S[5:4]));  // open: in1, in3, en
  Multiplexer #(.select(2), .width(32)) multiplexer_3 (
    .in0(_02), .in2(_22), .out(multiplexer_3_out), .sel(Switch__S[5:4]));  // open: in1, in3, en
  Multiplexer #(.select(2), .width(32)) multiplexer_4 (
    .in0(_03), .in2(_23), .out(multiplexer_4_out), .sel(Switch__S[5:4]));  // open: in1, in3, en
  Multiplexer #(.select(2)) multiplexer_5 (
    .in0(1'b0), .in1(1'b0), .in2(multiplexer_1_out), .in3(1'b0), .out(multiplexer_5_out), .sel(Switch__S[5:4]));  // open: en
  Multiplexer #(.select(2)) multiplexer_6 (
    .in0(multiplexer_5_out), .in1(1'b0), .in2(1'b0), .in3(1'b0), .out(Signed_Overflow), .sel(Switch__S[3:2]));  // open: en
  Multiplexer #(.select(4), .width(32)) multiplexer_7 (
    .in0(multiplexer_2_out), .in1(_21), .in2(multiplexer_3_out), .in3(multiplexer_4_out), .in4(_24),
    .in5(_25), .in8(jr), .in10(_2a), .in11(_2b), .in14(_3e), .in15(_3f), .out(RESULT), .sel(Switch__S[3:0]));  // open: in6, in7, in9, in12, in13, en

  // Other names for the same wires on the sheet: eq = Equal; overflow = Signed_Overflow; res[31:0] = RESULT;
  //   back2[1:0] = Switch__S[1:0]; back4[3:0] = Switch__S[3:0]; mid2[1:0] = Switch__S[3:2];
  //   front2[1:0] = Switch__S[5:4]

  // Notes on the sheet:
  //   INPUTS to your circuit
  //   INPUT to your circuit
  //   DON'T CHANGE THE INPUTS AND OUTPUTS! IF YOU DO SO, YOU NEED TO MAKE SURE THE PINS ARE IN THE RIGHT PLACES!
  //   OUTPUTS of your circuit
endmodule

module slt (
  input  [31:0] X,
  input  [31:0] Y,
  output [31:0] out
);

  wire Dif, Less, multiplexer_1_out, multiplexer_2_out, Sign;

  Multiplexer multiplexer_1 (.in0(Less), .in1(1'b1), .out(multiplexer_1_out), .sel(Dif));  // open: en
  Multiplexer multiplexer_2 (.in0(multiplexer_1_out), .in1(1'b0), .out(multiplexer_2_out), .sel(Sign));  // open: en
  Subtractor #(.width(1)) subtractor_1 (.a(X[31]), .b(Y[31]), .out(Dif), .bout(Sign));  // open: bin
  Subtractor #(.width(31)) subtractor_2 (.a(X[30:0]), .b(Y[30:0]), .bout(Less));  // open: out, bin
  assign out = {{31{1'b0}}, multiplexer_2_out};  // Bit_Extender bit_extender_1
endmodule

module sub (
  input  [31:0] X,
  input  [31:0] Y,
  output [31:0] result,
  output overflow
);

  wire overflowN;
  wire [31:0] adder_1_out, not_1_out;

  assign not_1_out = ~Y;  // NOT_Gate not_1, 32 bits wide
  Adder #(.width(32)) adder_1 (.a(not_1_out), .b(32'h1), .out(adder_1_out));  // open: cin, cout
  Multiplexer #(.select(2)) multiplexer_1 (
    .in0(1'b0), .in1(result[31]), .in2(overflowN), .in3(1'b0), .out(overflow), .sel({X[31], Y[31]}));  // open: en
  Adder #(.width(32)) adder_2 (.a(X), .b(adder_1_out), .out(result), .cout(overflowN));  // open: cin

  // Other names for the same wires on the sheet: Indicator[1:0] = {X[31], Y[31]}; signY = Y[31]; signX = X[31];
  //   overflowP = result[31]
endmodule

module sltu (
  input  [31:0] X,
  input  [31:0] Y,
  output [31:0] out
);

  wire subtractor_1_bout;

  Subtractor #(.width(32)) subtractor_1 (.a(X), .b(Y), .bout(subtractor_1_bout));  // open: out, bin
  assign out = {{31{1'b0}}, subtractor_1_bout};  // Bit_Extender bit_extender_1
endmodule

module bitpal (
  input  [31:0] X,
  output [31:0] out
);

  wire not_1_out, or_1_out, subtractor_1_bout, subtractor_2_bout;

  Subtractor #(.width(16)) subtractor_1 (
    .a({X[0], X[1], X[2], X[3], X[4], X[5], X[6], X[7], X[8], X[9], X[10], X[11], X[12], X[13], X[14], X[15]}),
    .b(X[31:16]), .bout(subtractor_1_bout));  // open: out, bin
  Subtractor #(.width(16)) subtractor_2 (
    .a(X[31:16]),
    .b({X[0], X[1], X[2], X[3], X[4], X[5], X[6], X[7], X[8], X[9], X[10], X[11], X[12], X[13], X[14], X[15]}),
    .bout(subtractor_2_bout));  // open: out, bin
  not not_1 (not_1_out, or_1_out);
  or or_1 (or_1_out, subtractor_1_bout, subtractor_2_bout);
  assign out = {{31{1'b0}}, not_1_out};  // Bit_Extender bit_extender_1

  // Other names for the same wires on the sheet: reverse[15:0] = {X[0], X[1], X[2], X[3], X[4], X[5], X[6], X[7], X[8], X[9], X[10], X[11], X[12], X[13], X[14], X[15]}
endmodule

module lfsr (
  input  [31:0] in_1,
  output [31:0] out
);

  wire xor_1_out, xor_3_out;

  xor xor_1 (xor_1_out, in_1[2], in_1[0]);
  xor xor_2 (out[31], in_1[5], xor_3_out);
  xor xor_3 (xor_3_out, in_1[3], xor_1_out);

  assign out[30:0] = in_1[31:1];
endmodule

module add (
  input  [31:0] X,
  input  [31:0] Y,
  output [31:0] out,
  output overflow
);

  wire not_1_out;

  Multiplexer #(.select(2)) multiplexer_1 (
    .in0(out[31]), .in1(1'b0), .in2(1'b0), .in3(not_1_out), .out(overflow), .sel({X[31], Y[31]}));  // open: en
  not not_1 (not_1_out, out[31]);
  Adder #(.width(32)) adder_1 (.a(X), .b(Y), .out(out));  // open: cin, cout

  // Other names for the same wires on the sheet: Indicator[1:0] = {X[31], Y[31]}; signY = Y[31]; signX = X[31];
  //   overflowP = out[31]
endmodule

module equal (
  input  [31:0] X,
  input  [31:0] Y,
  output out
);

  wire or_1_out, subtractor_1_bout, subtractor_2_bout;

  Subtractor #(.width(32)) subtractor_1 (.a(X), .b(Y), .bout(subtractor_1_bout));  // open: out, bin
  Subtractor #(.width(32)) subtractor_2 (.a(Y), .b(X), .bout(subtractor_2_bout));  // open: out, bin
  or or_1 (or_1_out, subtractor_1_bout, subtractor_2_bout);
  not not_1 (out, or_1_out);
endmodule
