// Logisim project cpu.circ as structural Verilog: 7 circuits, main circuit main
module main (
  input  [31:0] RS_READ_VALUE,
  input  [31:0] RT_READ_VALUE,
  input  [31:0] INSTRUCTION,
  input  CLOCK,
  input  RESET,
  output [31:0] t0,
  output [31:0] t1,
  output [31:0] t2,
  output [31:0] t3,
  output [4:0] RS,
  output [4:0] RT,
  output [4:0] Write_Register,
  output [31:0] RD_WRITE_VALUE,
  output RD_WRITE_ENABLE,
  output [23:0] FETCH_ADDRESS
);

  wire and_2_out, beq, bne, \byte , comparator_1_eq, demultiplexer_1_out0, demultiplexer_1_out1,
       demultiplexer_2_out0, demultiplexer_2_out1, demultiplexer_5_out0, demultiplexer_5_out2,
       demultiplexer_6_p5, demultiplexer_6_p6, I, J, jr, jump, kill, lb, lbu, link, load, lw, MemWrite,
       not_1_out, not_2_out, or_4_out, or_5_out, pcWrite, pcwrite_1_pcwrite, R, taken, temp_write, write;
  wire [0:0] or_7_out;
  wire [1:0] back2, front2, ts_1_read_rs, ts_1_read_rt, ts_1_write_rd;
  wire [3:2] back4;
  wire [4:0] Rd;
  wire [5:0] func;
  wire [15:6] imm;
  wire [23:0] adder_1_out, adder_2_out, bit_extender_2_out, bit_extender_3_out, multiplexer_7_out, newPC;
  wire [25:0] subtractor_1_out;
  wire [31:0] alu_i_type_1_result, ALU_result, bit_extender_1_out, linkRA, Mem_value, multiplexer_6_out,
       register_1_q, result, rs_data, rt_data, write_data, x_and_y_1_x, x_and_y_1_y;

  Multiplexer #(.width(5)) multiplexer_1 (.in0(Rd), .in1({5{1'b1}}), .out(Write_Register), .sel(link));  // open: en
  Multiplexer #(.width(32)) multiplexer_2 (
    .in0(write_data), .in1(linkRA), .out(RD_WRITE_VALUE), .sel(link));  // open: en
  Register #(.width(32)) register_1 (.D(INSTRUCTION), .Q(register_1_q), .clk(CLOCK));  // open: en, clr
  Multiplexer #(.width(32)) multiplexer_3 (
    .in0(register_1_q), .in1({32{1'b0}}), .out({front2, back4, back2, RS, RT, imm, func}), .sel(kill));  // open: en
  X_and_Y x_and_y_1 (
    .rs_data(rs_data), .rt_data(rt_data), .shamt(imm[10:6]), .func(func), .RT_read(RT_READ_VALUE),
    .RS_read(RS_READ_VALUE), .R(R), .rs(RS), .rt(RT), .X(x_and_y_1_x), .Y(x_and_y_1_y));
  ts ts_1 (.RS(RS), .RT(RT), .RD(Rd), .Read_rs(ts_1_read_rs), .Read_rt(ts_1_read_rt), .write_rd(ts_1_write_rd));
  alu_main ALU (
    .Switch__S(func), .X(x_and_y_1_x), .RESULT(ALU_result), .Y(x_and_y_1_y));  // open: Equal, Signed_Overflow
  ALU_i_type alu_i_type_1 (
    .imm({imm, func}), .op({front2, back4, back2}), .rs(x_and_y_1_x), .rt(x_and_y_1_y),
    .result(alu_i_type_1_result), .taken(taken));
  Multiplexer #(.width(32)) multiplexer_4 (
    .in0(ALU_result), .in1(alu_i_type_1_result), .out(result), .sel(I));  // open: en
  regfile_main RegFile (
    .Read_register_1(ts_1_read_rs), .Read_register_2(ts_1_read_rt), .write_register(ts_1_write_rd),
    .write_data(write_data), .t0_Value(t0), .t1_Value(t1), .t2_Value(t2), .t3_Value(t3),
    .RegWrite(temp_write), .clock(CLOCK), .Read_Data_1(rs_data), .Read_Data_2(rt_data));
  Multiplexer #(.width(32)) multiplexer_5 (.in0(result), .in1(Mem_value), .out(write_data), .sel(load));  // open: en
  Multiplexer #(.select(5), .width(32)) multiplexer_6 (
    .in0(RT_READ_VALUE), .in1(RT_READ_VALUE), .in2(RT_READ_VALUE), .in3(RT_READ_VALUE), .in4(RT_READ_VALUE),
    .in5(RT_READ_VALUE), .in6(RT_READ_VALUE), .in7(RT_READ_VALUE), .in8(rt_data), .in9(rt_data),
    .in10(rt_data), .in11(rt_data), .in12(RT_READ_VALUE), .in13(RT_READ_VALUE), .in14(RT_READ_VALUE),
    .in15(RT_READ_VALUE), .in16(RT_READ_VALUE), .in17(RT_READ_VALUE), .in18(RT_READ_VALUE),
    .in19(RT_READ_VALUE), .in20(RT_READ_VALUE), .in21(RT_READ_VALUE), .in22(RT_READ_VALUE),
    .in23(RT_READ_VALUE), .in24(RT_READ_VALUE), .in25(RT_READ_VALUE), .in26(RT_READ_VALUE),
    .in27(RT_READ_VALUE), .in28(RT_READ_VALUE), .in29(RT_READ_VALUE), .in30(RT_READ_VALUE),
    .in31(RT_READ_VALUE), .out(multiplexer_6_out), .sel(RT));  // open: en
  mem_main MEM (
    .Data_Mem_Addr(result), .Data_Mem_In(multiplexer_6_out), .ACCESS_BYTE(\byte ), .MEM_WRITE(MemWrite),
    .CLOCK(CLOCK), .Data_Mem_Out(Mem_value));
  pcWrite pcwrite_1 (.op({front2, back4, back2}), .pcWrite(pcwrite_1_pcwrite));
  or or_1 (load, lb, lbu, lw);
  Demultiplexer #(.enable("false")) demultiplexer_1 (
    .out0(demultiplexer_1_out0), .out1(demultiplexer_1_out1), .in(demultiplexer_2_out0), .sel(I));
  Demultiplexer #(.enable("false")) demultiplexer_2 (
    .out0(demultiplexer_2_out0), .out1(demultiplexer_2_out1), .in(1'b1), .sel(R));
  Demultiplexer #(.enable("false")) demultiplexer_3 (
    .out1(jr), .in(demultiplexer_2_out1), .sel(comparator_1_eq));  // open: out0
  Register #(.width(24)) register_2 (.D(multiplexer_7_out), .Q(FETCH_ADDRESS), .clk(CLOCK));  // open: en, clr
  or or_2 (pcWrite, pcwrite_1_pcwrite, taken, jr);
  or or_3 (\byte , lb, lbu);
  Demultiplexer #(.select(2), .enable("false")) demultiplexer_4 (
    .out2(jump), .out3(link), .in(demultiplexer_1_out0), .sel(back2));  // open: out0, out1
  Demultiplexer #(.select(2), .enable("false")) demultiplexer_5 (
    .out0(demultiplexer_5_out0), .out2(demultiplexer_5_out2), .in(demultiplexer_1_out1), .sel(front2));  // open: out1, out3
  Comparator #(.width(6), .mode("unsigned")) comparator_1 (
    .a(func), .b(6'b001000), .eq(comparator_1_eq));  // open: gt, lt
  // Demultiplexer #(.select(4), .enable("false")) demultiplexer_6: pin names not known; wires that end beside it: demultiplexer_5_out0, {back4, back2}, beq, bne, demultiplexer_6_p5, demultiplexer_6_p6
  Demultiplexer #(.select(4), .enable("false")) demultiplexer_7 (
    .out0(lb), .out3(lw), .out4(lbu), .out11(MemWrite), .in(demultiplexer_5_out2), .sel({back4, back2}));  // open: out1, out2, out5, out6, out7, out8, out9, out10, out12, out13, out14, out15
  Adder #(.width(24)) adder_1 (.a(FETCH_ADDRESS), .b(24'h1), .out(adder_1_out));  // open: cin, cout
  Multiplexer #(.width(24), .enable("false")) multiplexer_7 (
    .in0(adder_1_out), .in1(newPC), .out(multiplexer_7_out), .sel(pcWrite));
  selector selector_1 (.in_1({front2, back4, back2}), .I(I), .J(J), .R(R));
  getRD getrd_1 (.in_1({RS, RT, imm, func}), .write(write), .Rd(Rd), .R(R), .I(I));
  not not_1 (not_1_out, or_4_out);
  or or_4 (or_4_out, bne, jr, MemWrite, beq);
  not not_2 (not_2_out, write);
  assign bit_extender_1_out = {{8{1'b0}}, FETCH_ADDRESS};  // Bit_Extender bit_extender_1
  Bit_Extender #(.in_width(26), .out_width(24)) bit_extender_2 (.in(subtractor_1_out), .out(bit_extender_2_out));
  Subtractor #(.width(26)) subtractor_1 (
    .a({RS, RT, imm, func}), .b(26'h100000), .out(subtractor_1_out));  // open: bin, bout
  Adder #(.width(24)) adder_2 (.a(FETCH_ADDRESS), .b(bit_extender_3_out), .out(adder_2_out));  // open: cin, cout
  Bit_Extender #(.in_width(32), .out_width(24), .\type ("sign")) bit_extender_3 (.in(result), .out(bit_extender_3_out));
  Register #(.width(1)) register_3 (.D(or_5_out), .Q(kill), .clk(CLOCK));  // open: en, clr
  or or_5 (or_5_out, jump, link, jr, taken);
  and and_1 (temp_write, write, not_1_out);
  and and_2 (and_2_out, not_1_out, not_2_out);
  or or_6 (RD_WRITE_ENABLE, and_2_out, link);
  Adder #(.width(32)) adder_3 (.a(bit_extender_1_out), .b(32'h100000), .out(linkRA), .cin(1'b1));  // open: cout
  Multiplexer #(.select(3), .width(24)) multiplexer_8 (
    .in1(bit_extender_2_out), .in2(adder_2_out), .in4(bit_extender_3_out), .out(newPC),
    .sel({jr, taken, or_7_out[0]}));  // open: in0, in3, in5, in6, in7, en
  or or_7 (or_7_out[0], jump, link);

  // Other names for the same wires on the sheet: imm[5:0] = func; inst[25:0] = {RS, RT, imm, func};
  //   shamt[4:0] = imm[10:6]; back4[1:0] = back2; opcode[5:0] = {front2, back4, back2}; clk = CLOCK;
  //   nextPC[23:0] = FETCH_ADDRESS; r31 = link; rd_write = RD_WRITE_ENABLE; RS_value[31:0] = RS_READ_VALUE;
  //   RT_value[31:0] = RT_READ_VALUE; sw = MemWrite

  // Notes on the sheet:
  //   These are outputs/inputs from run.circ
  //   These are outputs to run.circ
  //   Feel free to move these components
endmodule

module selector (
  input  [5:0] in_1,
  output I,
  output J,
  output R
);

  wire comparator_1_eq, comparator_2_eq, comparator_3_eq, demultiplexer_1_out0, or_1_out;

  Comparator #(.width(6), .mode("unsigned")) comparator_1 (
    .a(in_1), .b({6{1'b0}}), .eq(comparator_1_eq));  // open: gt, lt
  Demultiplexer #(.enable("false")) demultiplexer_1 (
    .out0(demultiplexer_1_out0), .out1(R), .in(1'b1), .sel(comparator_1_eq));
  Comparator #(.width(6), .mode("unsigned")) comparator_2 (
    .a(in_1), .b(6'b000010), .eq(comparator_2_eq));  // open: gt, lt
  or or_1 (or_1_out, comparator_2_eq, comparator_3_eq);
  Demultiplexer #(.enable("false")) demultiplexer_2 (.out0(I), .out1(J), .in(demultiplexer_1_out0), .sel(or_1_out));
  Comparator #(.width(6), .mode("unsigned")) comparator_3 (
    .a(in_1), .b(6'b000011), .eq(comparator_3_eq));  // open: gt, lt
endmodule

module getRD (
  input  [25:0] in_1,
  input  R,
  input  I,
  output write,
  output [4:0] Rd
);

  wire and_1_out, comparator_1_lt, comparator_2_gt;
  wire [4:0] multiplexer_1_out;

  Multiplexer #(.width(5)) multiplexer_1 (
    .in0({5{1'b0}}), .in1(in_1[15:11]), .out(multiplexer_1_out), .sel(R));  // open: en
  Multiplexer #(.width(5)) multiplexer_2 (.in0(multiplexer_1_out), .in1(in_1[20:16]), .out(Rd), .sel(I));  // open: en
  Multiplexer multiplexer_3 (.in0(1'b0), .in1(1'b1), .out(write), .sel(and_1_out));  // open: en
  and and_1 (and_1_out, comparator_1_lt, comparator_2_gt);
  Comparator #(.width(5), .mode("unsigned")) comparator_1 (.a(5'b00111), .b(Rd), .lt(comparator_1_lt));  // open: gt, eq
  Comparator #(.width(5), .mode("unsigned")) comparator_2 (.a(5'b01100), .b(Rd), .gt(comparator_2_gt));  // open: eq, lt
endmodule

module ts (
  input  [4:0] RS,
  input  [4:0] RT,
  input  [4:0] RD,
  output [1:0] Read_rs,
  output [1:0] Read_rt,
  output [1:0] write_rd
);

  wire [4:0] subtractor_1_out, subtractor_2_out, subtractor_3_out;

  Subtractor #(.width(5)) subtractor_1 (.a(RS), .b(5'b01000), .out(subtractor_1_out));  // open: bin, bout
  Subtractor #(.width(5)) subtractor_2 (.a(RT), .b(5'b01000), .out(subtractor_2_out));  // open: bin, bout
  Subtractor #(.width(5)) subtractor_3 (.a(RD), .b(5'b01000), .out(subtractor_3_out));  // open: bin, bout
  Bit_Extender #(.in_width(5), .out_width(2)) bit_extender_1 (.in(subtractor_1_out), .out(Read_rs));
  Bit_Extender #(.in_width(5), .out_width(2)) bit_extender_2 (.in(subtractor_2_out), .out(Read_rt));
  Bit_Extender #(.in_width(5), .out_width(2)) bit_extender_3 (.in(subtractor_3_out), .out(write_rd));
endmodule

module X_and_Y (
  input  [31:0] RT_read,
  input  [31:0] RS_read,
  input  [31:0] rs_data,
  input  [31:0] rt_data,
  input  [4:0] rs,
  input  [4:0] rt,
  input  [4:0] shamt,
  input  [5:0] func,
  input  R,
  output [31:0] X,
  output [31:0] Y
);

  wire comparator_1_eq;
  wire [31:0] multiplexer_1_out, RT_F, shamt_t;

  assign shamt_t = {{27{1'b0}}, shamt};  // Bit_Extender bit_extender_1
  Multiplexer #(.width(32)) multiplexer_1 (
    .in0(RT_F), .in1(shamt_t), .out(multiplexer_1_out), .sel(comparator_1_eq));  // open: en
  Comparator #(.width(4), .mode("unsigned")) comparator_1 (
    .a(func[5:2]), .b(4'b0000), .eq(comparator_1_eq));  // open: gt, lt
  Multiplexer #(.select(5), .width(32)) multiplexer_2 (
    .in0(RS_read), .in1(RS_read), .in2(RS_read), .in3(RS_read), .in4(RS_read), .in5(RS_read), .in6(RS_read),
    .in7(RS_read), .in8(rs_data), .in9(rs_data), .in10(rs_data), .in11(rs_data), .in12(RS_read),
    .in13(RS_read), .in14(RS_read), .in15(RS_read), .in16(RS_read), .in17(RS_read), .in18(RS_read),
    .in19(RS_read), .in20(RS_read), .in21(RS_read), .in22(RS_read), .in23(RS_read), .in24(RS_read),
    .in25(RS_read), .in26(RS_read), .in27(RS_read), .in28(RS_read), .in29(RS_read), .in30(RS_read),
    .in31(RS_read), .out(X), .sel(rs));  // open: en
  Multiplexer #(.width(32)) multiplexer_3 (.in0(RT_F), .in1(multiplexer_1_out), .out(Y), .sel(R));  // open: en
  Multiplexer #(.select(5), .width(32)) multiplexer_4 (
    .in0(RT_read), .in1(RT_read), .in2(RT_read), .in3(RT_read), .in4(RT_read), .in5(RT_read), .in6(RT_read),
    .in7(RT_read), .in8(rt_data), .in9(rt_data), .in10(rt_data), .in11(rt_data), .in12(RT_read),
    .in13(RT_read), .in14(RT_read), .in15(RT_read), .in16(RT_read), .in17(RT_read), .in18(RT_read),
    .in19(RT_read), .in20(RT_read), .in21(RT_read), .in22(RT_read), .in23(RT_read), .in24(RT_read),
    .in25(RT_read), .in26(RT_read), .in27(RT_read), .in28(RT_read), .in29(RT_read), .in30(RT_read),
    .in31(RT_read), .out(RT_F), .sel(rt));  // open: en

  // Other names for the same wires on the sheet: funt[5:0] = func; RS_F[31:0] = X
endmodule

module ALU_i_type (
  input  [31:0] rs,
  input  [31:0] rt,
  input  [15:0] imm,
  input  [5:0] op,
  output taken,
  output [31:0] result
);

  wire comparator_1_eq, comparator_2_eq, not_1_out;
  wire [31:0] addiu, andi, beq, bne, l_s_address, multiplexer_1_out, ori, signEx, zeroEx;

  Multiplexer #(.select(4), .width(32)) multiplexer_1 (
    .in0({32{1'b0}}), .in1({32{1'b0}}), .in2({32{1'b0}}), .in3({32{1'b0}}), .in4(beq), .in5(bne),
    .in6({32{1'b0}}), .in7({32{1'b0}}), .in8({32{1'b0}}), .in9(addiu), .in10({32{1'b0}}), .in11({32{1'b0}}),
    .in12(andi), .in13(ori), .in14({32{1'b0}}), .in15({imm, {16{1'b0}}}), .out(multiplexer_1_out),
    .sel(op[3:0]));  // open: en
  assign zeroEx = {{16{1'b0}}, imm};  // Bit_Extender bit_extender_1
  assign signEx = {{16{imm[15]}}, imm};  // Bit_Extender bit_extender_2
  Multiplexer #(.select(2), .width(32)) multiplexer_2 (
    .in0(multiplexer_1_out), .in2(l_s_address), .out(result), .sel(op[5:4]));  // open: in1, in3, en
  Adder #(.width(32)) adder_1 (.a(rs), .b(signEx), .out(addiu));  // open: cin, cout
  assign andi = rs & zeroEx;  // AND_Gate and_1, 32 bits wide
  assign ori = rs | zeroEx;  // OR_Gate or_1, 32 bits wide
  Adder #(.width(32)) adder_2 (.a(rs), .b(signEx), .out(l_s_address));  // open: cin, cout
  Comparator #(.width(32), .mode("unsigned")) comparator_1 (.a(rs), .b(rt), .eq(comparator_1_eq));  // open: gt, lt
  not not_1 (not_1_out, comparator_2_eq);
  Comparator #(.width(32), .mode("unsigned")) comparator_2 (.a(rs), .b(rt), .eq(comparator_2_eq));  // open: gt, lt
  Multiplexer #(.width(32)) multiplexer_3 (
    .in0({32{1'b0}}), .in1(signEx), .out(beq), .sel(comparator_1_eq));  // open: en
  Multiplexer #(.width(32)) multiplexer_4 (.in0({32{1'b0}}), .in1(signEx), .out(bne), .sel(not_1_out));  // open: en
  Multiplexer #(.select(4)) multiplexer_5 (
    .in0(1'b0), .in1(1'b0), .in2(1'b0), .in3(1'b0), .in4(comparator_1_eq), .in5(not_1_out), .in6(1'b0),
    .in7(1'b0), .in8(1'b0), .in9(1'b0), .in10(1'b0), .in11(1'b0), .in12(1'b0), .in13(1'b0), .in14(1'b0),
    .in15(1'b0), .out(taken), .sel(op[3:0]));  // open: en

  // Other names for the same wires on the sheet: lui[31:16] = imm; back4[3:0] = op[3:0]; front2[1:0] = op[5:4]
endmodule

module pcWrite (
  input  [5:0] op,
  output pcWrite
);

  wire comparator_1_eq, comparator_2_eq;

  Comparator #(.width(6), .mode("unsigned")) comparator_1 (
    .a(op), .b(6'b000010), .eq(comparator_1_eq));  // open: gt, lt
  Comparator #(.width(6), .mode("unsigned")) comparator_2 (
    .a(op), .b(6'b000011), .eq(comparator_2_eq));  // open: gt, lt
  or or_1 (pcWrite, comparator_1_eq, comparator_2_eq);
endmodule
